# Fritzing sketch Simple DC driver for test (saved by Fritzing 0.9.2b)
breadboards: 1

parts:
  VCC1 = 4 x AAA Battery Mount
  D1 = Diode [package=diode-1n4148]
  M1 = DC Motor

nets:
  GND: VCC1.-, D1.C, M1.pin_2
  N1: VCC1.+, D1.A, M1.pin_1
